# Fritzing sketch Current sensor (saved by Fritzing 0.9.10b)
breadboards: 1

parts:
  Raspberry_Pi = Raspberry Pi 2
  TRS1 = Audio Jack (TRS) 3.5mm [package="PG203J [THT]"]
  C3 = Electrolytic Capacitor [capacitance=10µF voltage=50V package="100 mil [THT, electrolytic]"]
  R1 = Resistor [tolerance=±5% power=0.5W resistance=100k package=THT]
  R2 = Resistor [tolerance=±5% power=0.5W resistance=100k package=THT]
  ADC = MCP3008 [package=dil16]
  TRS2 = Audio Jack (TRS) 3.5mm [package="PG203J [THT]"]
  C4 = Electrolytic Capacitor [capacitance=10µF voltage=50V package="100 mil [THT, electrolytic]"]
  R3 = Resistor [tolerance=±5% power=0.5W resistance=100k package=THT]
  R4 = Resistor [tolerance=±5% power=0.5W resistance=100k package=THT]
  Motor_clamp_meter = Transformer [package=transformer]
  Light_clamp_meter = Transformer [package=transformer]

nets:
  3V3: Raspberry_Pi.3v3, Raspberry_Pi.3V3, R2.Pin_0, ADC.VREF, ADC.VDD, R4.Pin_0
  N1: Raspberry_Pi.GPIO10, ADC.Din
  N2: Raspberry_Pi.GPIO9, ADC.Dout
  N3: Raspberry_Pi.GPIO11, ADC.CLK
  N4: Raspberry_Pi.GND, C3.-, R1.Pin_0, ADC.DGND, ADC.AGND, C4.-, R3.Pin_0
  N5: Raspberry_Pi.GPIO8, ADC.CS/SHDN
  N6: TRS1.Sleeve, C3.+, R1.Pin_1, R2.Pin_1, Motor_clamp_meter.4
  N7: TRS1.Tip, ADC.CH0, Motor_clamp_meter.1
  N8: ADC.CH1, TRS2.Tip, Light_clamp_meter.1
  N9: TRS2.Sleeve, C4.+, R3.Pin_1, R4.Pin_1, Light_clamp_meter.4
